# Fritzing sketch electrical-schema (saved by Fritzing 0.9.0b)
breadboards: 1

parts:
  part = Arduino Uno (Rev3)
  R1 = Resistor [tolerance=±5% resistance=220 package=THT]
  R2 = Resistor [tolerance=±5% resistance=220 package=THT]
  R3 = Resistor [tolerance=±5% resistance=220 package=THT]
  R4 = Resistor [tolerance=±5% resistance=220 package=THT]
  R5 = Resistor [tolerance=±5% resistance=220 package=THT]
  LED6 = LED - 5mm [color="Red (633nm)" package="5 mm [THT]"]
  LED7 = LED - 5mm [color="Green (555nm)" package="5 mm [THT]"]
  LED3 = LED - 5mm [color="Green (555nm)" package="5 mm [THT]"]
  LED4 = LED - 5mm [color="Yellow (574nm)" package="5 mm [THT]"]
  LED5 = LED - 5mm [color="Red (633nm)" package="5 mm [THT]"]
  R6 = Resistor [tolerance=±5% resistance=220 package=THT]
  LED8 = LED - 5mm [color="Red (633nm)" package="5 mm [THT]"]
  R7 = Resistor [tolerance=±5% resistance=220 package=THT]
  LED9 = LED - 5mm [color="Red (633nm)" package="5 mm [THT]"]
  R8 = Resistor [tolerance=±5% resistance=220 package=THT]
  LED10 = LED - 5mm [color="Red (633nm)" package="5 mm [THT]"]
  R9 = Resistor [tolerance=±5% resistance=220 package=THT]
  LED11 = LED - 5mm [color="Red (633nm)" package="5 mm [THT]"]
  10_x = Resistor [tolerance=±5% resistance=220 package=THT]
  LED12 = LED - 5mm [color="Red (633nm)" package="5 mm [THT]"]

nets:
  N1: part.D8, R3.Pin_0
  N2: part.D9_PWM, R4.Pin_0
  N3: part.D10_PWM/SS, R5.Pin_0
  N4: part.D11_PWM/MOSI, R8.Pin_0
  N5: part.D12/MISO, R9.Pin_0
  N6: part.D13/SCK, 10_x.Pin_0
  GND: part.GND, LED6.cathode, LED7.cathode, LED3.cathode, LED4.cathode, LED5.cathode, LED8.cathode, LED9.cathode, LED10.cathode, LED11.cathode, LED12.cathode
  N7: part.D4, R1.Pin_0
  N8: part.D5_PWM, R2.Pin_0
  N9: part.D6_PWM, R6.Pin_0
  N10: part.D7, R7.Pin_0
  N11: R1.Pin_1, LED7.anode
  N12: R2.Pin_1, LED6.anode
  N13: R3.Pin_1, LED3.anode
  N14: R4.Pin_1, LED4.anode
  N15: R5.Pin_1, LED5.anode
  N16: R6.Pin_1, LED8.anode
  N17: R7.Pin_1, LED9.anode
  N18: R8.Pin_1, LED10.anode
  N19: R9.Pin_1, LED11.anode
  N20: 10_x.Pin_1, LED12.anode
